// Digital circuit DRAM.dig as structural Verilog
module DRAM (
  input  clk,
  input  read,
  input  write,
  input  [14:0] addr,
  input  [47:0] idata,
  output done,
  output [47:0] odata
);

  wire or_1_out;
  wire [47:0] DRAM_d;

  or or_1 (or_1_out, read, write);
  RAMDualPort #(.AddrBits(15), .Bits(48)) DRAM (.A(addr), .Din(idata), .str(write), .C(clk), .ld(read), .D(DRAM_d));
  Register register_1 (.D(or_1_out), .C(clk), .en(1'b1), .Q(done));
  Register #(.Bits(48)) register_2 (.D(DRAM_d), .C(clk), .en(read), .Q(odata));
endmodule
