// Digital circuit MESM.dig as structural Verilog
module MESM (
  input  \int ,
  input  clk
);

  wire acc_is_zero, ALU_done, ALU_doneNext, ALU_NOP, and_1_out, and_2_out, and_3_out, and_4_out, and_11_out,
       and_12_out, and_13_out, and_14_out, and_15_out, and_16_out, and_17_out, and_18_out, and_19_out,
       and_20_out, and_21_out, and_23_out, and_24_out, and_25_out, and_26_out, branch, busy, C_active,
       C_sel_mem, C_write, comparator_1_eq, comparator_2_eq, comparator_3_eq, comparator_4_eq,
       comparator_5_eq, comparator_6_eq, comparator_8_eq, comparator_9_eq, comparator_12_eq, dbus_done,
       dbus_read, dbus_write, decode, gie, ibus_done, ibus_fetch, irq, isOpCached, M_i_is_zero, m_w,
       multiplexer_4_out, multiplexer_7_out, multiplexer_14_out, nor_1_out, not_1_out, not_2_out, not_3_out,
       not_4_out, not_5_out, not_6_out, not_7_out, not_8_out, not_9_out, not_10_out, not_11_out, not_12_out,
       not_13_out, not_14_out, not_15_out, not_16_out, not_17_out, not_18_out, not_19_out, not_20_out,
       not_21_out, not_22_out, op_lflag, or_1_out, or_2_out, or_3_out, or_4_out, or_5_out, or_8_out,
       or_10_out, or_11_out, P_A_NEG, P_A_NONZERO, P_A_ZERO, P_BRANCH, P_DECODE, P_ENTER_INT, P_EXIT_INT,
       P_M_NONZERO, P_M_W, P_M_ZERO, P_OP_NOT_CACHED, P_R_ADD, P_SEL_ADDR, P_SEL_ALU_MEM, P_W_A, P_W_C,
       P_W_OPCODE, P_W_PC, register_1_q, register_2_q, reset, w_acc, w_opcode, w_pc;
  wire [0:0] PC;
  wire [1:0] P_SEL_MR, P_SEL_MW;
  wire [2:0] op_scmd, P_SEL_ACC, P_SEL_MD, P_SEL_PC;
  wire [3:0] add_4_s, ALU_count, multiplexer_13_out, multiplexer_15_out, multiplexer_16_out, op_ir, op_lcmd,
       reg_index;
  wire [5:0] ALU_op, R_q;
  wire [8:0] add_1_s, entry16_d, entry64_d, multiplexer_1_out, multiplexer_2_out, multiplexer_3_out,
       multiplexer_6_out, multiplexer_8_out, multiplexer_9_out, multiplexer_10_out, P_IMM, uPC_q;
  wire [11:0] opcode;
  wire [14:0] add_3_s, add_6_s, C_q, dbus_addr, ibus_addr, M_i, M_r, M_regs_da, M_regs_db,
       multiplexer_18_out, multiplexer_24_out, multiplexer_29_out, multiplexer_30_out, op_addr, pcCached_q,
       sub_1_s, U_addr, V_addr;
  wire [15:0] add_5_s, multiplexer_26_out, multiplexer_27_out, multiplexer_28_out;
  wire [23:0] opCache_q, opCache_q_2;
  wire [31:0] cycles_out;
  wire [47:0] ACC, ALU_B, ALU_result, ALU_y, and_22_out, dbus_idata, DRAM_d, ibus_idata, IROM_d,
       multiplexer_17_out, multiplexer_19_out, multiplexer_20_out, multiplexer_31_out, or_9_out, xor_1_out, Y;
  wire [48:0] ALU_sum;
  wire [50:0] multiplexer_11_out, uROM_d;

  ROM #(.AddrBits(6), .Bits(9)) entry64 (.A({op_lcmd[2:0], op_scmd}), .sel(1'b1), .D(entry64_d));
  ROM #(.AddrBits(4), .Bits(9)) entry16 (.A(op_lcmd), .sel(1'b1), .D(entry16_d));
  Comparator #(.Bits(24)) comparator_1 (
    .a({op_ir, op_lflag, op_lcmd, op_scmd, opcode}), .b(24'h90000), .eq(comparator_1_eq));  // open: gt, lt
  Comparator #(.Bits(24)) comparator_2 (
    .a({op_ir, op_lflag, op_lcmd, op_scmd, opcode}), .b(24'h8000), .eq(comparator_2_eq));  // open: gt, lt
  Comparator #(.Bits(24)) comparator_3 (
    .a({op_ir, op_lflag, op_lcmd, op_scmd, opcode}), .b(24'h22000), .eq(comparator_3_eq));  // open: gt, lt
  or or_1 (or_1_out, comparator_1_eq, comparator_2_eq, comparator_3_eq);
  not not_1 (not_1_out, C_active);
  Multiplexer #(.Bits(9)) multiplexer_1 (.sel(op_lflag), .in_0(entry64_d), .in_1(entry16_d), .out(multiplexer_1_out));
  and and_1 (and_1_out, or_1_out, not_1_out);
  Multiplexer #(.Bits(9)) multiplexer_2 (
    .sel(and_1_out), .in_0(multiplexer_1_out), .in_1(9'h16), .out(multiplexer_2_out));
  not not_2 (not_2_out, busy);
  Multiplexer #(.Bits(9)) multiplexer_3 (.sel(irq), .in_0(multiplexer_2_out), .in_1(9'h17), .out(multiplexer_3_out));
  and and_2 (and_2_out, \int , gie);
  and and_3 (and_3_out, P_ENTER_INT, not_2_out);
  and and_4 (and_4_out, not_2_out, P_EXIT_INT);
  Multiplexer multiplexer_4 (.sel(reset), .in_0(and_2_out), .in_1(1'b0), .out(multiplexer_4_out));
  Multiplexer #(.Bits(15)) multiplexer_5 (
    .sel(op_lflag), .in_0({{3{op_lcmd[3]}}, opcode}), .in_1({op_scmd, opcode}), .out(op_addr));
  Add #(.Bits(9)) add_1 (.a(9'h1), .b(uPC_q), .c_i(1'b0), .s(add_1_s));  // open: c_o
  or or_2 (or_2_out, reset, and_3_out);
  or or_3 (or_3_out, and_4_out, reset, and_3_out);
  Multiplexer #(.Bits(9)) multiplexer_6 (
    .sel(decode), .in_0(add_1_s), .in_1(multiplexer_3_out), .out(multiplexer_6_out));
  Register u_irq (.D(multiplexer_4_out), .C(clk), .en(1'b1), .Q(irq));
  Multiplexer multiplexer_7 (.sel(or_2_out), .in_0(and_4_out), .in_1(1'b0), .out(multiplexer_7_out));
  Multiplexer #(.Bits(9)) multiplexer_8 (.sel(branch), .in_0(multiplexer_6_out), .in_1(P_IMM), .out(multiplexer_8_out));
  Register u_gie (.D(multiplexer_7_out), .C(clk), .en(or_3_out), .Q(gie));
  Register #(.Bits(9)) uPC (.D(multiplexer_10_out), .C(clk), .en(1'b1), .Q(uPC_q));
  Multiplexer #(.Bits(9)) multiplexer_9 (.sel(busy), .in_0(multiplexer_8_out), .in_1(uPC_q), .out(multiplexer_9_out));
  Multiplexer #(.Bits(9)) multiplexer_10 (
    .sel(reset), .in_0(multiplexer_9_out), .in_1({9{1'b1}}), .out(multiplexer_10_out));
  ROM #(.AddrBits(9), .Bits(51)) uROM (.A(multiplexer_10_out), .sel(1'b1), .D(uROM_d));
  Multiplexer #(.Bits(51)) multiplexer_11 (.sel(reset), .in_0(uROM_d), .in_1({51{1'b0}}), .out(multiplexer_11_out));
  not not_3 (not_3_out, busy);
  not not_4 (not_4_out, busy);
  not not_5 (not_5_out, busy);
  and and_5 (m_w, not_3_out, P_M_W);
  and and_6 (w_acc, not_4_out, P_W_A);
  and and_7 (C_write, not_5_out, P_W_C);
  Register #(.Bits(51)) uop (
    .D(multiplexer_11_out), .C(clk), .en(1'b1),
    .Q({P_SEL_ALU_MEM, P_M_ZERO, P_W_PC, P_EXIT_INT, P_ENTER_INT, C_active, P_BRANCH, P_A_ZERO, P_A_NEG, P_A_NONZERO, P_W_C, P_W_A, dbus_write, dbus_read, P_DECODE, P_W_OPCODE, ibus_fetch, P_OP_NOT_CACHED, C_sel_mem, P_R_ADD, P_SEL_ADDR, P_SEL_PC, P_M_NONZERO, P_SEL_MR, P_M_W, P_SEL_MW, P_SEL_MD, P_SEL_ACC, ALU_op, P_IMM}));
  not not_6 (not_6_out, busy);
  not not_7 (not_7_out, busy);
  and and_8 (w_opcode, not_6_out, P_W_OPCODE);
  and and_9 (w_pc, not_7_out, P_W_PC);
  not not_8 (not_8_out, busy);
  or or_4 (or_4_out, dbus_read, dbus_write);
  not not_9 (not_9_out, dbus_done);
  not not_10 (not_10_out, ibus_done);
  Comparator #(.Bits(6)) comparator_4 (.a(ALU_op), .b({6{1'b0}}), .eq(comparator_4_eq));  // open: gt, lt
  not not_11 (not_11_out, ALU_done);
  not not_12 (not_12_out, isOpCached);
  not not_13 (not_13_out, acc_is_zero);
  not not_14 (not_14_out, M_i_is_zero);
  and and_10 (decode, not_8_out, P_DECODE);
  and and_11 (and_11_out, or_4_out, not_9_out);
  and and_12 (and_12_out, ibus_fetch, not_10_out);
  not not_15 (not_15_out, comparator_4_eq);
  and and_13 (and_13_out, not_12_out, P_OP_NOT_CACHED);
  and and_14 (and_14_out, acc_is_zero, P_A_ZERO);
  and and_15 (and_15_out, not_13_out, P_A_NONZERO);
  and and_16 (and_16_out, M_i_is_zero, P_M_ZERO);
  and and_17 (and_17_out, not_14_out, P_M_NONZERO);
  and and_18 (and_18_out, ACC[40], P_A_NEG);
  and and_19 (and_19_out, not_15_out, not_11_out);
  or or_5 (or_5_out, and_13_out, and_14_out, and_15_out, and_16_out, and_17_out);
  or or_6 (busy, and_11_out, and_12_out, and_19_out);
  Reset #(.invertOutput("false")) rst (.out(reset));
  or or_7 (branch, or_5_out, and_18_out, P_BRANCH);
  Comparator #(.Bits(24)) comparator_5 (
    .a({op_ir, op_lflag, op_lcmd, op_scmd, opcode}), .b(24'h6d94e5), .eq(comparator_5_eq));  // open: gt, lt
  Comparator #(.Bits(24)) comparator_6 (
    .a({op_ir, op_lflag, op_lcmd, op_scmd, opcode}), .b(24'h2dfd63), .eq(comparator_6_eq));  // open: gt, lt
  // Probe on {op_ir, op_lflag, op_lcmd, op_scmd, opcode}
  // Probe on ACC
  // Probe on Y
  // Probe on {ibus_addr, PC[0]}
  // Probe on ibus_addr
  // Probe on ibus_idata
  // Probe on dbus_idata
  // Probe on dbus_read
  // Probe on dbus_write
  // Probe on dbus_addr
  Multiplexer #(.Bits(48)) multiplexer_12 (
    .sel(P_SEL_ALU_MEM), .in_0({{41{1'b0}}, U_addr[6:0]}), .in_1(dbus_idata), .out(ALU_B));
  and and_20 (and_20_out, comparator_5_eq, P_DECODE);
  and and_21 (and_21_out, comparator_6_eq, P_DECODE);
  Register register_1 (.D(and_20_out), .C(clk), .en(nor_1_out), .Q(register_1_q));
  Register register_2 (.D(and_21_out), .C(clk), .en(nor_1_out), .Q(register_2_q));
  Counter #(.Bits(32)) cycles (.en(nor_1_out), .C(clk), .clr(1'b0), .out(cycles_out));  // open: ovf
  not not_16 (not_16_out, ALU_done);
  // Probe on cycles_out
  nor nor_1 (nor_1_out, register_1_q, register_2_q);
  Add #(.Bits(48)) add_2 (.a(ACC), .b(ALU_B), .c_i(1'b0), .s(ALU_sum[47:0]), .c_o(ALU_sum[48]));
  or or_8 (or_8_out, ALU_NOP, not_16_out);
  LED testPass (.in(register_1_q));
  LED testFail (.in(register_2_q));
  assign and_22_out = ACC & ALU_B;  // And and_22, 48 bits wide
  assign or_9_out = ACC | ALU_B;  // Or or_9, 48 bits wide
  assign xor_1_out = ACC ^ ALU_B;  // XOr xor_1, 48 bits wide
  Register #(.Bits(6)) R (.D(6'b000001), .C(clk), .en(1'b0), .Q(R_q));
  Multiplexer #(.Bits(4)) multiplexer_13 (.sel(ALU_NOP), .in_0(add_4_s), .in_1(4'b0000), .out(multiplexer_13_out));
  Multiplexer multiplexer_14 (.sel(ALU_NOP), .in_0(ALU_doneNext), .in_1(1'b0), .out(multiplexer_14_out));
  Multiplexer #(.Selector_Bits(2), .Bits(4)) multiplexer_15 (
    .sel(P_SEL_MW), .in_0(reg_index), .in_1(P_IMM[3:0]), .in_2(V_addr[3:0]), .in_3(U_addr[3:0]),
    .out(multiplexer_15_out));
  Multiplexer #(.Selector_Bits(2), .Bits(4)) multiplexer_16 (
    .sel(P_SEL_MR), .in_0(reg_index), .in_1(P_IMM[3:0]), .in_2(V_addr[3:0]), .in_3(U_addr[3:0]),
    .out(multiplexer_16_out));
  or or_10 (or_10_out, ALU_NOP, not_17_out);
  not not_17 (not_17_out, ALU_done);
  Add #(.Bits(15)) add_3 (.a(M_r), .b(15'h1), .c_i(1'b0), .s(add_3_s));  // open: c_o
  Sub #(.Bits(15)) sub_1 (.a(M_r), .b(15'h1), .c_i(1'b0), .s(sub_1_s));  // open: c_o
  Register #(.Bits(4)) count (.D(multiplexer_13_out), .C(clk), .en(or_10_out), .Q(ALU_count));
  Register done (.D(multiplexer_14_out), .C(clk), .en(or_8_out), .Q(ALU_done));
  Comparator #(.Bits(6)) comparator_7 (.a({6{1'b0}}), .b(ALU_op), .eq(ALU_NOP));  // open: gt, lt
  ROM #(.AddrBits(15), .Bits(48)) IROM (.A(ibus_addr), .sel(1'b1), .D(IROM_d));
  Multiplexer #(.Selector_Bits(3), .Bits(48)) multiplexer_17 (
    .sel(P_SEL_ACC), .in_0(ALU_result), .in_1(dbus_idata), .in_2({{33{1'b0}}, M_r}),
    .in_3({{42{1'b0}}, R_q}), .in_4(Y), .in_5(ALU_result), .in_6(ALU_result), .in_7(ALU_result),
    .out(multiplexer_17_out));
  Multiplexer #(.Selector_Bits(3), .Bits(15)) multiplexer_18 (
    .sel(P_SEL_MD), .in_0(ibus_addr), .in_1(ACC[14:0]), .in_2(M_r), .in_3(add_3_s), .in_4(sub_1_s),
    .in_5(V_addr), .in_6(U_addr), .in_7(U_addr), .out(multiplexer_18_out));
  Add #(.Bits(4)) add_4 (.a(4'b0001), .b(ALU_count), .c_i(1'b0), .s(add_4_s));  // open: c_o
  Multiplexer #(.Bits(48), .Selector_Bits(2)) multiplexer_19 (
    .sel(ALU_op[1:0]), .in_0(ALU_result), .in_1(and_22_out), .in_2(or_9_out), .in_3(xor_1_out),
    .out(multiplexer_19_out));
  not not_18 (not_18_out, ALU_NOP);
  not not_19 (not_19_out, ALU_done);
  Multiplexer #(.Selector_Bits(2), .Bits(48)) multiplexer_20 (
    .sel(ALU_op[1:0]), .in_0(ALU_y), .in_1({48{1'b0}}), .in_2({48{1'b0}}), .in_3(ACC),
    .out(multiplexer_20_out));
  Multiplexer #(.Selector_Bits(2)) multiplexer_21 (
    .sel(ALU_op[1:0]), .in_0(ALU_done), .in_1(1'b1), .in_2(1'b1), .in_3(1'b1), .out(ALU_doneNext));
  Register done_2 (.D(ibus_fetch), .C(clk), .en(1'b1), .Q(ibus_done));
  // Probe on P_SEL_ACC
  RegisterFile #(.AddrBits(4), .Bits(15)) M_regs (
    .Din(multiplexer_18_out), .we(m_w), .Rw(multiplexer_15_out), .C(clk), .Ra(reg_index),
    .Rb(multiplexer_16_out), .Da(M_regs_da), .Db(M_regs_db));
  and and_23 (and_23_out, not_18_out, not_19_out);
  not not_20 (not_20_out, ALU_NOP);
  and and_24 (and_24_out, not_20_out, not_21_out);
  not not_21 (not_21_out, ALU_done);
  not not_22 (not_22_out, ibus_done);
  Register #(.Bits(48)) u_ACC (.D(multiplexer_17_out), .C(clk), .en(w_acc), .Q(ACC));
  Register #(.Bits(48)) u_Y (.D(48'h1), .C(clk), .en(1'b0), .Q(Y));
  Comparator #(.Bits(4)) comparator_8 (.a(4'b0000), .b(multiplexer_16_out), .eq(comparator_8_eq));  // open: gt, lt
  Comparator #(.Bits(4)) comparator_9 (.a(4'b0000), .b(reg_index), .eq(comparator_9_eq));  // open: gt, lt
  Register #(.Bits(48)) u_ALU_result (.D(multiplexer_19_out), .C(clk), .en(and_23_out), .Q(ALU_result));
  and and_25 (and_25_out, ibus_fetch, not_22_out);
  Multiplexer #(.Bits(15)) multiplexer_22 (.sel(comparator_8_eq), .in_0(M_regs_db), .in_1({15{1'b0}}), .out(M_r));
  Multiplexer #(.Bits(15)) multiplexer_23 (.sel(comparator_9_eq), .in_0(M_regs_da), .in_1({15{1'b0}}), .out(M_i));
  Register #(.Bits(48)) u_ALU_y (.D(multiplexer_20_out), .C(clk), .en(and_24_out), .Q(ALU_y));
  Comparator #(.Bits(48)) comparator_10 (.a({48{1'b0}}), .b(ACC), .eq(acc_is_zero));  // open: gt, lt
  Comparator #(.Bits(15)) comparator_11 (.a({15{1'b0}}), .b(M_i), .eq(M_i_is_zero));  // open: gt, lt
  Register #(.Bits(48)) register_3 (.D(IROM_d), .C(clk), .en(and_25_out), .Q(ibus_idata));
  Add #(.Bits(16)) add_5 (.a({ibus_addr, PC[0]}), .b(16'h1), .c_i(1'b0), .s(add_5_s));  // open: c_o
  Multiplexer #(.Bits(15)) multiplexer_24 (
    .sel(C_sel_mem), .in_0(U_addr), .in_1(dbus_idata[14:0]), .out(multiplexer_24_out));
  and and_26 (and_26_out, decode, isOpCached);
  Multiplexer #(.Bits(15)) multiplexer_25 (.sel(P_SEL_ADDR), .in_0(U_addr), .in_1(M_r), .out(dbus_addr));
  Multiplexer #(.Selector_Bits(3), .Bits(16)) multiplexer_26 (
    .sel(P_SEL_PC), .in_0({U_addr, 1'b0}), .in_1({V_addr, 1'b0}), .in_2({M_i, 1'b0}),
    .in_3({{6{1'b0}}, P_IMM, 1'b0}), .in_4(add_5_s), .in_5({U_addr, 1'b0}), .in_6({U_addr, 1'b0}),
    .in_7({U_addr, 1'b0}), .out(multiplexer_26_out));
  Multiplexer #(.Bits(16)) multiplexer_27 (
    .sel(and_26_out), .in_0({ibus_addr, PC[0]}), .in_1(add_5_s), .out(multiplexer_27_out));
  Register #(.Bits(15)) C (.D(multiplexer_24_out), .C(clk), .en(C_write), .Q(C_q));
  RAMDualPort #(.AddrBits(15), .isProgramMemory("true"), .Bits(48)) DRAM (
    .A(dbus_addr), .Din(ACC), .str(dbus_write), .C(clk), .ld(dbus_read), .D(DRAM_d));
  Comparator #(.Bits(15)) comparator_12 (.a(dbus_addr), .b({15{1'b0}}), .eq(comparator_12_eq));  // open: gt, lt
  Multiplexer #(.Bits(16)) multiplexer_28 (
    .sel(w_pc), .in_0(multiplexer_27_out), .in_1(multiplexer_26_out), .out(multiplexer_28_out));
  Add #(.Bits(15)) add_6 (.a(op_addr), .b(C_q), .c_i(1'b0), .s(add_6_s));  // open: c_o
  or or_11 (or_11_out, dbus_read, dbus_write);
  Multiplexer #(.Bits(15)) multiplexer_29 (.sel(P_R_ADD), .in_0(V_addr), .in_1(M_r), .out(multiplexer_29_out));
  Multiplexer #(.Bits(15)) multiplexer_30 (.sel(C_active), .in_0(op_addr), .in_1(add_6_s), .out(multiplexer_30_out));
  Multiplexer #(.Bits(48)) multiplexer_31 (
    .sel(comparator_12_eq), .in_0(DRAM_d), .in_1({48{1'b0}}), .out(multiplexer_31_out));
  Register #(.Bits(16)) u_PC (.D(multiplexer_28_out), .C(clk), .en(1'b1), .Q({ibus_addr, PC[0]}));
  Register #(.Bits(48)) opCache (.D(ibus_idata), .C(clk), .en(w_opcode), .Q({opCache_q_2, opCache_q}));
  Register #(.Bits(15)) pcCached (.D(ibus_addr), .C(clk), .en(w_opcode), .Q(pcCached_q));
  Register register_4 (.D(or_11_out), .C(clk), .en(1'b1), .Q(dbus_done));
  Register #(.Bits(48)) register_5 (.D(multiplexer_31_out), .C(clk), .en(dbus_read), .Q(dbus_idata));
  Multiplexer #(.Bits(24)) multiplexer_32 (
    .sel(PC[0]), .in_0(opCache_q_2), .in_1(opCache_q), .out({op_ir, op_lflag, op_lcmd, op_scmd, opcode}));
  Comparator #(.Bits(15)) comparator_13 (.a(pcCached_q), .b(ibus_addr), .eq(isOpCached));  // open: gt, lt
  Add #(.Bits(15)) add_7 (.a(multiplexer_29_out), .b(M_i), .c_i(1'b0), .s(U_addr));  // open: c_o
  Register #(.Bits(15)) u_V_addr (.D(multiplexer_30_out), .C(clk), .en(decode), .Q(V_addr));
  Register #(.Bits(4)) u_reg_index (.D(op_ir), .C(clk), .en(decode), .Q(reg_index));

  // Other names for the same wires on the sheet: P_ALU[5:0] = ALU_op; P_SEL_C_MEM = C_sel_mem; P_FETCH = ibus_fetch;
  //   P_MEM_R = dbus_read; P_MEM_W = dbus_write; P_C_ACTIVE = C_active; ALU_A[47:0] = ACC; acc_is_neg = ACC[40];
  //   interrupt = \int ; opcode[23:12] = {op_ir, op_lflag, op_lcmd, op_scmd}; op_scmd[5:3] = op_lcmd[2:0];
  //   PC[15:1] = ibus_addr

  // Notes on the sheet:
  //   contents of entry64 (hex, n*v repeats v):
  //   19,1b,1f,20,24,25,26,27,28,2a,2d,30,33,34,37,38,39,3a,3b,3c,3d,3e,3f,42,43,44,46,
  //   47,48,49,4a,4c,4d,4e,52,53,55,56,57,58,59,5a,5b,5c,5d,5e,5f,60,61,62,63,64,65,66,
  //   67,68,69,6a,6b,6c,6d,6e,6f,70
  //   contents of entry16 (hex, n*v repeats v):
  //   71,72,73,75,77,78,79,7d,81,83,85,86,87,8b,8f,90
  //   Command decoder
  //   Interrupt request latch
  //   Interrupts enable register
  //   Microcode sequencer
  //   contents of uROM (hex, n*v repeats v):
  //   a40000,8001010000,a40001,a40002,a40003,a40004,a40005,a40006,a40007,a40008,a40009,
  //   a4000a,a4000b,a4000c,a4000d,a4000e,a4000f,1800018000001,c00000000,1000000000,c00000000,
  //   201000000000,1200000012,400000000000,1200000012,4000000000,1200000012,4000000000,
  //   1b0000f,a04100800f,1200000012,1200000012,404100000f,1ac000f,a000008000,1200000012,
  //   1200000012,1200000012,1200000012,1200000012,a000008000,1200000012,2000008000,4008000000200,
  //   1200000012,2000008000,4008000000600,1200000012,2000008000,4008000000a00,1200000012,
  //   1200000012,2000008000,4008000000400,1200000012,1200000012,1200000012,1200000012,1200000012,
  //   1200000012,1200000012,1200000012,1200000012,2000008000,4008000000800,1200000012,1200000012,
  //   1200000012,8000020000,1200000012,1200000012,1200000012,1200000012,1200000012,8000000800,
  //   1200000012,1200000012,1200e40012,e40000,1b0000f,a04100800f,1200000012,9203010012,
  //   4041ac000f,9203010012,1200c80012,1282d80012,1200000012,1200000012,1200000012,1200000012,
  //   1200000012,1200000012,1200000012,1200000012,1200000012,1200000012,1200000012,1200000012,
  //   1200000012,1200000012,1200000012,1200000012,1200000012,1200000012,1200000012,1200000012,
  //   1200000012,1200000012,1200000012,1200000012,1200000012,1200000012,1200000012,1200000012,
  //   10000000000,201200000014,12100000000,201200000014,1200940012,1200980012,8000000007b,
  //   1200000012,1000000000000,1200000012,2000000007f,1200000012,1000000000000,1200000012,
  //   1000000000000,1200000012,1000008800000,1200000012,1200000012,1200000012,2000000000089,
  //   1200000012,1000008000000,1200000012,400008d,1200000012,1000008000000,1200000012,1200000012,
  //   4000092,1200000012,10000088c0000,1200000012
  //   Accumulator
  //   Instruction ROM
  //   contents of IROM (hex, n*v repeats v):
  //   0,840c009000,b800b00840c,940c00a40c,b800b00840d,940d00a40d,b800b00840d,940e0b800b,
  //   840d00d40e,a40c0b800b,6d94e5090000,2dfd63090000
  //   M index registers
  //   Execution Address logic
  //   Programm Counter
  //   Data RAM
endmodule
